# Fritzing sketch OV5642_Schematic (saved by Fritzing 0.9.3b)
breadboards: 1

parts:
  OV5642_Camera = DIP - 8 pins [chip_label=OV5642 package="DIP (Dual Inline) [THT]"]
  Raspberry_Pi_1 = Raspberry Pi 3 [part_number=RPI-3-V1.2]
  U1 = LM1085 Voltage Regulator [part_number=LM1085 chip_label=LM1085 package="SIP (Single Inline) [THT]"]
  R1 = Resistor [tolerance=±5% resistance=5k package=THT]
  R2 = Resistor [tolerance=±5% resistance=15k package=THT]
  C1 = Tantalum Capacitor [capacitance=10µF package="100 mil [THT, tantalum]"]
  Vin = DC Power [voltage=5]
  C2 = Electrolytic Capacitor [capacitance=10µF package="100 mil [THT, electrolytic]"]

nets:
  N1: OV5642_Camera.CS, Raspberry_Pi_1.GIPO17
  N2: OV5642_Camera.MOSI, Raspberry_Pi_1.GIPO10
  N3: OV5642_Camera.MISO, Raspberry_Pi_1.GIPO9
  N4: OV5642_Camera.SCLK, Raspberry_Pi_1.GIPO11
  GND: OV5642_Camera.GND, Raspberry_Pi_1.GND
  N5: OV5642_Camera.VCC, U1.OUT, R1.Pin_1, C1.+
  N6: OV5642_Camera.SDA, Raspberry_Pi_1.GPIO2
  N7: OV5642_Camera.SCL, Raspberry_Pi_1.GPIO3
  N8: U1.Vin, Vin.V+, C2.+
  N9: U1.ADJ, R1.Pin_0, R2.Pin_1
  GND_2: R2.Pin_0, C1.-, Vin.V-, C2.-

custom parts:
  DIP - 8 pins: Basic IC for the OV5642 Digial Camera. Includes the 8 pins with labels.
  LM1085 Voltage Regulator: LM1085 Voltage Regulator in DIP 3 Package. Basi Pins with Labels.
