# Fritzing sketch RFM95roughdraft (saved by Fritzing 0.9.10b)
breadboards: 1

parts:
  RFM95 = Adafruit RFM9x LoRa Radio [part_number="Adafruit #3072 and #3073"]
  RPI_4B = Raspberry Pi 4B  # not connected
  VR1 = MCP1826-ADJ [chip_label=MCP1826 package="SIP (Single Inline) [THT]"]
  V1 = DC Power [voltage=5V]
  C1 = Ceramic Capacitor [capacitance=4.7µF voltage=20V package="100 mil [THT, multilayer]"]
  C2 = Ceramic Capacitor [capacitance=1µF voltage=20V package="100 mil [THT, multilayer]"]
  R1 = Resistor [tolerance=±5% power=0.25 resistance=71k package=THT]
  R2 = Resistor [tolerance=±5% power=0.25 resistance=10k package=THT]

nets:
  N1: RFM95.VIN, VR1.Vout, C2.1, R1.Pin_1
  GND: RFM95.GND, VR1.GND, V1.V-, C1.0, C2.0, R2.Pin_1
  N2: VR1.VIN, V1.V+, C1.1
  N3: VR1.ADJ, R1.Pin_0, R2.Pin_0

custom parts:
  Adafruit RFM9x LoRa Radio: Sending data over long distances is like magic, and now you can be a magician with this range of powerful and easy-to-use radio modules. Sure, sometimes you want to talk to a computer (a good time to use WiFi) or perhaps communicate with a Phone (choose Bluetooth Low Energy!) but what if you want to send data very far? Most WiFi, Bluetooth, Zigbee and other wireless chipsets use 2.4GHz, which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
  MCP1826-ADJ: MCP1826-ADJ Voltage Regulator in dip 5 package. Basic Pins of Voltage Regulator in IC package.
